# Fritzing sketch sketch (saved by Fritzing 0.9.3b)
breadboards: 1

parts:
  Part1 = Arduino Nano (Rev3.0)
  Part2 = Arduino Uno (Rev3)
  U1 = RF-LINK_TX [package=rf-link_tx]
  U2 = RF-LINK_RX [package=rf-link_rx]

nets:
  GND: Part1.GND, U2.GND
  N1: Part1.D12/MISO, U2.Data
  5V: Part1.5V, U2.VCC
  5V_2: Part2.5V, U1.+5V
  GND_2: Part2.GND, U1.GND

custom parts:
  RF-LINK_TX: Common RF transmitter of the 315.00Mhz varity
  RF-LINK_RX: RF Link receivers- WRL-8947, 8948, 8949, 8950
